# Fritzing sketch EspDustLogger (saved by Fritzing 0.9.8b)
circuit board: 8.46667cm x 5.64444cm

parts:
  Q1 = NPN-Transistor [part_number=BC547B package="TO92 [THT]"]
  R1 = Resistor [tolerance=±5% power=0.25 resistance=10k package=THT]
  Q2 = NPN-Transistor [part_number=BC547B package="TO92 [THT]"]
  R2 = Resistor [tolerance=±5% power=0.25 resistance=1k package=THT]
  R3 = Resistor [tolerance=±5% power=0.25 resistance=1k package=THT]
  R4 = Resistor [tolerance=±5% power=0.25 resistance=1k package=THT]
  S1 = Pushbutton [part_number=Bootstrap package="[THT]"]
  R5 = Resistor [tolerance=±5% power=0.25 resistance=1k package=THT]
  U1 = ESP32S-HiLetgo [part_number=ESP32]
  J1 = JST-B3P-VH [part_number="IKEA Connection" package=THT]

nets:
  GND: Q1.E, Q2.E, S1.Pin_1, S1.Pin_2, U1.GND, J1.pin1
  N1: Q1.B, R1.Pin_1
  N2: Q1.C, R2.Pin_0, R4.Pin_1
  N3: R1.Pin_0, J1.pin2
  N4: Q2.B, R2.Pin_1
  N5: Q2.C, R3.Pin_1, U1.GPIO25
  N6: R3.Pin_0, R5.Pin_0, U1.3.3
  N7: R4.Pin_0, U1.VIN, J1.pin3
  N8: S1.Pin_3, S1.Pin_4, R5.Pin_1, U1.GPIO35

notes:
  +5V
  GND
  REST

custom parts:
  ESP32S-HiLetgo: HiLetgo ESP-WROOM-32 ESP32 ESP-32S Development Board 2.4GHz Dual-Mode WiFi + Bluetooth Dual Cores Microcontroller The ESP32 integrated with Antenna switches, RF Balun, power amplifiers, low-noise amplifiers, filters, and management modules, and the entire solution occupies the least area of PCB. 2.4 GHz Wi-Fi plus Bluetooth dual-mode chip, with TSMC Ultra-low power consumption 40nm technology,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
